// Logisim project LATCH (S-R).circ as structural Verilog: 2 circuits, main circuit main
module main (
  input  in_1,
  input  in_2,
  output out_3,
  output out_4
);

  nor nor_1 (out_3, in_1, out_4);
  nor nor_2 (out_4, out_3, in_2);
endmodule

module S_R_LATCH (
);

  main main_1 ();  // open: in_1, in_2, out_3, out_4
endmodule
